# Fritzing sketch sketch_scheme (saved by Fritzing 0.9.4)

parts:
  U1 = ESP8266 ESP-01 Upgraded WiFi Module [part_number=ESP8266]
  Arduino_Nano = Arduino Nano (Rev3.0)
  V1 = DC Power [voltage=5]
  U2 = Voltage Regulator - 3.3V [package="TO220 [THT]"]
  R2 = Resistor [tolerance=±5% resistance=1k package="0603 [SMD]"]
  R3 = Resistor [tolerance=±5% resistance=1k package="0603 [SMD]"]
  R4 = Resistor [tolerance=±5% resistance=10k package="0603 [SMD]"]
  R5 = Resistor [tolerance=±5% resistance=10k package="0603 [SMD]"]
  R6 = Resistor [tolerance=±5% resistance=10k package="0603 [SMD]"]
  S1 = SWITCH-MOMENTARY-2 [package=tactile_switch_smd]
  R7 = Resistor [tolerance=±5% resistance=10k package="0603 [SMD]"]
  S2 = SWITCH-MOMENTARY-2 [package=tactile_switch_smd]
  R1 = Resistor [tolerance=±5% resistance=1k package="0603 [SMD]"]

nets:
  N1: U1.RXD, R2.Pin_0, R1.Pin_1
  N2: U1.VCC, U2.output_voltage, R5.Pin_0, R6.Pin_0
  N3: U1.GPIO_0, R7.Pin_0
  N4: U1.RST/GPIO_16, R6.Pin_1
  N5: U1.CH_PD, R5.Pin_1
  GND: U1.GND, Arduino_Nano.GND, V1.V-, U2.GND, R3.Pin_1, S1.2, S2.2
  N6: U1.TXD, Arduino_Nano.D1/TX
  N7: Arduino_Nano.D0/RX, R1.Pin_0
  N8: Arduino_Nano.RESET, R4.Pin_0
  N9: Arduino_Nano.5V, V1.V+, U2.input_voltage
  N10: R2.Pin_1, R3.Pin_0
  N11: R4.Pin_1, S2.1
  N12: S1.1, R7.Pin_1

custom parts:
  ESP8266 ESP-01 Upgraded WiFi Module: Upgraded Version ESP-01,all Flash are upgraded to 1M byte.Also support Cloud service remote transmission.
